# Fritzing sketch schematic (saved by Fritzing 0.9.3b)
breadboards: 1

parts:
  Part1 = Arduino Uno (Rev3)
  Pitch = Trimmer Potentiometer [maximum_resistance=10kΩ package=THT]
  Mod = Trimmer Potentiometer [maximum_resistance=10kΩ package=THT]
  ToneLength = Trimmer Potentiometer [maximum_resistance=10kΩ package=THT]
  Noise = Toggle Switch [package=THT]
  Ramp = Toggle Switch [package=THT]
  Saw = Toggle Switch [package=THT]
  Square = Toggle Switch [package=THT]
  Triangle = Toggle Switch [package=THT]
  Sine = Toggle Switch [package=THT]
  1kohm = Resistor [tolerance=±5% resistance=220 package=THT]
  1k = Resistor [tolerance=±5% resistance=220 package=THT]
  1k_2 = Resistor [tolerance=±5% resistance=220 package=THT]
  1k_3 = Resistor [tolerance=±5% resistance=220 package=THT]
  1k_4 = Resistor [tolerance=±5% resistance=220 package=THT]
  1k_5 = Resistor [tolerance=±5% resistance=220 package=THT]
  SequenceInterval = Trimmer Potentiometer [maximum_resistance=10kΩ package=THT]
  LED1 = LED - 5mm [color="Red (633nm)" package="5 mm [THT]"]
  R1 = Resistor [tolerance=±5% resistance=220 package=THT]
  Ultrasonic_Sensor = SPM0204UD5 [package=spm0204ud5]
  4-way_switch = SWITCH-DPDT [package=es]  # not connected

nets:
  N1: Part1.A0, Pitch.wiper
  N2: Part1.A1, ToneLength.wiper
  N3: Part1.A2, Mod.wiper
  N4: Part1.A3, SequenceInterval.wiper
  N5: Part1.D9_PWM, R1.Pin_1
  N6: Part1.D12/MISO, Ultrasonic_Sensor.GND#
  N7: Part1.D13/SCK, Ultrasonic_Sensor.VS
  N8: Part1.D2, Sine.L2, 1k_5.Pin_0
  N9: Part1.D3_PWM, Triangle.L2, 1k_4.Pin_0
  N10: Part1.D4, Square.L2, 1k_3.Pin_0
  N11: Part1.D5_PWM, Saw.L2, 1k_2.Pin_0
  N12: Part1.D6_PWM, Ramp.L2, 1k.Pin_0
  N13: Part1.D7, Noise.L2, 1kohm.Pin_0
  N14: Part1.5V, Pitch.leg1, Mod.leg1, ToneLength.leg1, Noise.COM, Ramp.COM, Saw.COM, Square.COM, Triangle.COM, Sine.COM, SequenceInterval.leg1
  N15: Part1.GND, Pitch.leg2, Mod.leg2, ToneLength.leg2, 1kohm.Pin_1, 1k.Pin_1, 1k_2.Pin_1, 1k_3.Pin_1, 1k_4.Pin_1, 1k_5.Pin_1, SequenceInterval.leg2, LED1.cathode
  N16: LED1.anode, R1.Pin_0

// code stored in the sketch: mysynth.ino
// Arduino synth library absolute frequency example

//Hardware cHIGHnectiHIGHs:

//                    +10�F
//PIN 11 ---[ 1k ]--+---||--->> Audio out
//                  |
//                 === 10nF
//                  |
//                 GND

#include <StandardCplusplus.h>
#include <synth.h>
// IMPORT POWER LIBRARY
#include <vector>
#define trig 13
#define echo 12
const int pitchpin = A0; // Pitch Pot (analog)
const int tonelengthpin = A1; // Tone Length Pot (analog)
const int modpin = A2; // Mod pot (analog)
// Waveform switches
const int switch1 = 2; // sine
const int switch2 = 3; // triangle
const int switch3 = 4; // square 
const int switch4 = 5; // saw
const int switch5 = 6; // ramp 
const int switch6 = 7; // noise
//Envelopes
const int envelopeswitch = 8 // 4-way envelope switch (or potentially another pot)
const int sequenceinterval = A3; // Sequence Interval Pot (analog)
const int LEDPin = 9;

synth edgar;    //-Make a synth

void update() {
  // use 6 arduino toggle switches to choose SINE,TRIANGLE,SQUARE,SAW,RAMP,NOISE
  // add a pot for pitch (5th parameter in setupVoice)
  int pitch = analogRead(pitchpin);
  int tonelength = analogRead(tonelengthpin);
  int mod = analogRead(modpin);
  //setupVoice( voice[0-3] , waveform[SINE,TRIANGLE,SQUARE,SAW,RAMP,NOISE] , pitch[0-127], envelope[ENVELOPE0-ENVELOPE3], length[0-127], mod[0-127, 64=no mod])

  char switch1state = digitalRead(switch1);
  char switch2state = digitalRead(switch2);
  char switch3state = digitalRead(switch3);
  char switch4state = digitalRead(switch4);
  char switch5state = digitalRead(switch5);
  char switch6state = digitalRead(switch6);
  int envelope = analogRead(envelopeswitch); // not sure what the output of the 4-way switch will be. if cant figure out, use a pot for envelope and threshold
  switch (envelope) {
    case 1:
      envel = ENVELOPE0;
    case 2:
      envel = ENVELOPE1;
    case 3:
      envel = ENVELOPE2;
    case 4:
      envel = ENVELOPE3;
  }

  char switchstates[] = {switch1state, switch2state, switch3state, switch4state, switch5state, switch6state};
  Serial.println(switchstates);
  std::vector< int > onswitches;
  for (int i = 0; i < 6; i++) {
    if (switchstates[i] == "HIGH") {
      onswitches.push_back(i);
    }
  }
  int onsize = sizeof(onswitches) / sizeof(int);
  for (int i = 0; i < onsize + 1; i++) {
    edgar.setupVoice(i, onswitches[i], pitch, envel, tonelength, mod); // second parameter: 0,1,2,3,4,5 = SINE,TRIANGLE,SQUARE,SAW,RAMP,NOISE
  }
}
void setup() {
  edgar.begin(); //-Start it up
  update();
  pinMode(OUTPUT, LEDPin);
  digitalWrite(LEDPin, HIGH);
  // ADD CALL TO POWER LIBRARY FOR TIMEOUT DURATION (MAKE IT SOMETHING LIKE 3 HRS)
}
void loop()
{
  digitalWrite(trig, LOW);
  delayMicroseconds(2);
  digitalWrite(trig, HIGH);
  delayMicroseconds(10);
  digitalWrite(trig, LOW);
  duration = pulseIn(echo, HIGH);
  distance = microsecondsToCentimeters(duration);

  // tone(8, distance, 40); pin 8 is the piezo out
  sequenceaddition = analogRead(sequenceinterval);
  for (int i = 0; i < onsize + 1; i++) {
    edgar.setFrequency(i, distance + (sequenceaddition * i));
    edgar.trigger(i);
  }
  //  if (millis() % 1000 == 0) {
//    update(); // update switch configurations to see if they've been changed, every second
//  }
  update();
  // ADD CALL TO THE POWER LIBRARY TO CHECK IF TIMEOUT
}
